# Fritzing sketch Overall (saved by Fritzing 0.8.7b)
breadboards: 1

parts:
  ARDUINO = Arduino Mega ADK (Rev3)
  IR15 = TSOP312.., 314.. [part_number=TSOP31240 package=THT]
  IR14 = TSOP312.., 314.. [part_number=TSOP31240 package=THT]
  IR13 = TSOP312.., 314.. [part_number=TSOP31240 package=THT]
  12 = TSOP312.., 314.. [part_number=TSOP31240 package=THT]
  IR11 = TSOP312.., 314.. [part_number=TSOP31240 package=THT]
  IR10 = TSOP312.., 314.. [part_number=TSOP31240 package=THT]
  IR9 = TSOP312.., 314.. [part_number=TSOP31240 package=THT]
  IR8 = TSOP312.., 314.. [part_number=TSOP31240 package=THT]
  IR7 = TSOP312.., 314.. [part_number=TSOP31240 package=THT]
  IR6 = TSOP312.., 314.. [part_number=TSOP31240 package=THT]
  IR5 = TSOP312.., 314.. [part_number=TSOP31240 package=THT]
  IR4 = TSOP312.., 314.. [part_number=TSOP31240 package=THT]
  IR3 = TSOP312.., 314.. [part_number=TSOP31240 package=THT]
  IR2 = TSOP312.., 314.. [part_number=TSOP31240 package=THT]
  IR1 = TSOP312.., 314.. [part_number=TSOP31240 package=THT]
  FrontUS = SRF05 Ultrasonic Rangefinder
  LeftUS = SRF05 Ultrasonic Rangefinder
  BackUS = SRF05 Ultrasonic Rangefinder
  RightUS = SRF05 Ultrasonic Rangefinder

nets:
  N1: ARDUINO.D14/TX3, IR15.Data
  GND: ARDUINO.GND, IR15.GND, IR14.GND, IR13.GND, 12.GND, IR11.GND, IR10.GND, IR9.GND, IR8.GND, IR7.GND, IR6.GND, IR5.GND, IR4.GND, IR3.GND, IR2.GND, IR1.GND, FrontUS.GND, LeftUS.GND, BackUS.GND, RightUS.GND
  N2: ARDUINO.D13_PWM, IR14.Data
  N3: ARDUINO.D12_PWM, IR13.Data
  N4: ARDUINO.D11_PWM, 12.Data
  N5: ARDUINO.D10_PWM, IR11.Data
  N6: ARDUINO.D9_PWM, IR10.Data
  N7: ARDUINO.D8_PWM, IR9.Data
  VCC: ARDUINO.5V, IR15.Vs, IR14.Vs, IR13.Vs, 12.Vs, IR11.Vs, IR10.Vs, IR9.Vs, IR8.Vs, IR7.Vs, IR6.Vs, IR5.Vs, IR4.Vs, IR3.Vs, IR2.Vs, IR1.Vs, LeftUS.VCC, BackUS.VCC, RightUS.VCC
  N8: ARDUINO.D0/RX0, IR1.Data
  N9: ARDUINO.D1/TX0, IR2.Data
  N10: ARDUINO.D2_PWM, IR3.Data
  N11: ARDUINO.D3_PWM, IR4.Data
  N12: ARDUINO.D4_PWM, IR5.Data
  N13: ARDUINO.D5_PWM, IR6.Data
  N14: ARDUINO.D6_PWM, IR7.Data
  N15: ARDUINO.D7_PWM, IR8.Data
